# Fritzing sketch schema (saved by Fritzing 0.9.3b)
breadboards: 1

parts:
  Raspberry_Pi_1 = Raspberry Pi 3 [part_number=RPI-3-V1.2]
  HC-SR04_Sensor_1 = HC-SR04 Ultrasonic Distance Sensor
  S1 = H-Bridge with L298N
  M2 = DC Motor
  M4 = DC Motor
  R1 = Resistor [tolerance=±5% resistance=1k package=THT]
  R2 = Resistor [tolerance=±1% resistance=2k package=THT]
  VCC6 = Battery
  M6 = DC Motor
  M7 = DC Motor
  VCC7 = Battery
  VCC8 = Battery

nets:
  N1: Raspberry_Pi_1.GPIO4, S1.IN4
  GND: Raspberry_Pi_1.GND, HC-SR04_Sensor_1.GND, S1.GND, R2.Pin_1, VCC7.-
  N2: Raspberry_Pi_1.GPIO17, S1.IN3
  N3: Raspberry_Pi_1.GPIO27, S1.IN2
  N4: Raspberry_Pi_1.GPIO22, S1.IN1
  N5: Raspberry_Pi_1.GPIO12, S1.ENB
  N6: Raspberry_Pi_1.GPIO24, R1.Pin_0, R2.Pin_0
  N7: Raspberry_Pi_1.GPIO23, HC-SR04_Sensor_1.TRIG
  N8: Raspberry_Pi_1.GPIO18, S1.ENA
  5V: Raspberry_Pi_1.5V, HC-SR04_Sensor_1.VCC, S1.5V
  N9: HC-SR04_Sensor_1.ECHO, R1.Pin_1
  N10: S1.12V, VCC6.+
  N11: S1.M1-01, M6.pin_2, M7.pin_2
  N12: S1.M1-02, M6.pin_1, M7.pin_1
  N13: S1.M2-01, M2.pin_1, M4.pin_1
  N14: S1.M2-02, M2.pin_2, M4.pin_2
  N15: VCC6.-, VCC8.+
  N16: VCC7.+, VCC8.-

custom parts:
  H-Bridge with L298N: h-bridge
